// Logisim project R32_CPU.circ as structural Verilog: 1 circuit, main circuit R32_CPU
module R32_CPU (
);

  Clock CLK ();  // open: out
  Adder #(.width(16)) PC___1 ();  // open: a, b, out, cin, cout
  RAM #(.addrWidth(4), .dataWidth(16)) RAM_regs__port_A ();  // open: addr, data, sel, clk, ld, clr
  RAM #(.addrWidth(4), .dataWidth(16)) RAM_regs__port_B ();  // open: addr, data, sel, clk, ld, clr
  Register #(.width(16)) PC ();  // open: D, en, Q, clk, clr
  Multiplexer #(.select_bits(2), .width(16)) MUX_PC_suivant ();  // open: in0, in1, out, sel
  Multiplexer #(.select_bits(2), .width(4)) adr_A__rd_SP_LR ();  // open: in0, in1, out, sel
  Multiplexer #(.select_bits(2), .width(4)) adr_B__rs_SP_rd ();  // open: in0, in1, out, sel
  Multiplexer #(.select_bits(1), .width(4)) adr_W__rd_SP ();  // open: in0, in1, out, sel
  Multiplexer #(.select_bits(2), .width(16)) adr__imm_rb_ALU ();  // open: in0, in1, out, sel
  ROM #(.addrWidth(15), .dataWidth(32)) ROM_programme_32K_32 ();  // open: addr, data
  ROM #(.addrWidth(8), .dataWidth(24)) \ROM_contrôle_256_24  ();  // open: addr, data
  RAM #(.addrWidth(16), .dataWidth(16)) \RAM_données  ();  // open: addr, data, sel, clk, ld, clr
  Adder #(.width(16)) ADD ();  // open: a, b, out, cin, cout
  Subtractor #(.width(16)) SUB ();  // open: a, b, out, bin, bout
  // AND_Gate and_1 is placed but not wired
  // OR_Gate or_1 is placed but not wired
  // XOR_Gate xor_1 is placed but not wired
  Decoder #(.select_bits(4)) DECODE_sauts ();  // open: out0, out1, sel, en
  Shifter #(.width(16)) SHL ();  // open: in, dist, out
  Shifter #(.width(16)) SHR ();  // open: in, dist, out
  Multiplexer #(.select_bits(2), .width(16)) WB__ALU_RAM_PC_1 ();  // open: in0, in1, out, sel
  // NOT_Gate not_1 is placed but not wired
  // AND_Gate and_2 is placed but not wired
  // OR_Gate or_2 is placed but not wired
  Multiplexer #(.select_bits(1), .width(16)) \opérande_B__rb_imm  ();  // open: in0, in1, out, sel
  Multiplexer #(.select_bits(3), .width(16)) \MUX_résultat_ALU  ();  // open: in0, in1, out, sel
  Register #(.width(4), .trigger("falling")) Flags_ZNVC ();  // open: D, en, Q, clk, clr

  // Notes on the sheet:
  //   ZONE 1 — FETCH (séquencement)
  //   Le PC de Logisim compte les INSTRUCTIONS (pas les mots).
  //   PC_mots = 2 × PC_logisim. Chaque ROM 32 bits = 1 instruction (W0 + W1).
  //   ZONE 2 — DÉCODAGE ET CONTRÔLE (le moteur figé)
  //   La ROM de contrôle est une fonction pure de l'opcode : adresse=opcode, sortie=mot 24 bits.
  //   Voir LOGISIM.md pour la table complète (copier-coller dans l'éditeur de la ROM).
  //   ZONE 3 — BANC DE REGISTRES (16 × 16 bits, 2 lectures + 1 écriture)
  //   Deux RAM 16×16 identiques (ports A et B) écrites ensemble = 2 ports de lecture.
  //   L'écriture dans R0 est bloquée par we_regfile AND (wr_addr != 0).
  //   ZONE 5 — MÉMOIRE DONNÉES 64K×16 + ECRITURE REGISTRES
  //   LÉGENDE DU MOT DE CONTRÔLE (24 bits)
  //   [23:20] alu_op   [19] halt   [18] branch   [17:16] pc_src (00=PC+1, 01=imm16, 10=LR)
  //   [15:14] wb_sel (00=ALU, 01=RAM, 10=PC+1)   [13] we_mem   [12] we_flags   [11] we_regfile
  //   [10] alu_b_sel (0=rb, 1=imm16)   [9:8] mem_addr (00=imm, 01=rb, 10=ALU)
  //   [7:6] ra_addr (00=rd, 01=SP, 10=LR)   [5:4] rb_addr (00=rs, 01=SP, 10=rd)   [3] wr_addr (0=rd, 1=SP)
  //   POP (0x1A) = seule instruction à 2 coups d'horloge : voir LOGISIM.md (état FSM).
  //   Registre 16 bits, chargé à chaque coup d'horloge
  //   we_mem=1 : écrit ra dans RAM[adr]   |   we_regfile=1 : RF[adr W] <- WB
  //   00=PC+1  01=imm16 (saut)  10=LR (RET)
  //   Clic droit > Load Image : charger build/xxx_logisim.hex
  //   ZONE 4 — ALU 16 bits
  //   alu_op[2:0] : 0=PASS B  1=ADD  2=SUB  3=AND  4=OR  5=XOR  6=SHL  7=SHR
  //   ZONE 6 — MMIO (0xF000-0xFFFF) : UART + debug décimal
  //   adr >= 0xF000 : rediriger vers les registres UART (FPGA : décodeur d'adresses).
  //   0xF000=data  0xF001=status  0xF002=debug décimal
  //   Splitter : W0[15:0] -> opcode[7:0] rd[11:8] rs[15:12]
  //              W1[31:16] = imm16
  //   opcode[3:0] : 1=JMP 2=JZ 3=JNZ 4=JN 5=JC 6=JV
  //   Chargé quand we_flags=1 (bits V Z N C de l'ALU)
endmodule
